# Fritzing sketch 베터리 l298n 배선 (saved by Fritzing 0.9.10b)

parts:
  VCC1 = Battery
  S1 = H-Bridge with L298N
  부품1 = Arduino Mega 2560 (Rev3)

nets:
  GND: VCC1.-, S1.GND, 부품1.GND
  N1: VCC1.+, S1.12V
  5V: S1.5V, 부품1.5V

custom parts:
  Battery: Your standard 2x 18650 battery pack (7,4 Volts)
  H-Bridge with L298N: h-bridge
