# Fritzing sketch l298n_motor (saved by Fritzing 0.9.10b)

parts:
  VCC1 = Battery
  S1 = H-Bridge with L298N
  부품1 = Arduino Mega 2560 (Rev3)

nets:
  GND: VCC1.-, S1.GND, 부품1.GND
  N1: VCC1.+, S1.12V
  5V: S1.5V, 부품1.5V
  N2: S1.ENA, 부품1.D8_PWM
  N3: S1.IN1, 부품1.D9_PWM
  N4: S1.IN2, 부품1.D10_PWM
  N5: S1.IN3, 부품1.D11_PWM
  N6: S1.IN4, 부품1.D12_PWM
  N7: S1.ENB, 부품1.D13_PWM

custom parts:
  Battery: Your standard 2x 18650 battery pack (7,4 Volts)
  H-Bridge with L298N: h-bridge
